// Logisim project td4_cpu.circ as structural Verilog: 3 circuits, main circuit main
module main (
  input  in_1,
  input  IM_1,
  input  IM_2,
  input  in_4,
  input  IM_3,
  input  IM_4,
  input  in_7,
  input  in_8,
  input  CK,
  input  A,
  input  B
);

  wire A_74HC161_qa, A_74HC161_qb, A_74HC161_qc, A_74HC161_qd, B_74HC161_qa, B_74HC161_qb, B_74HC161_qc,
       B_74HC161_qd, C_74HC161_qa, C_74HC161_qb, C_74HC161_qc, C_74HC161_qd, custom_74hc283_1_c4,
       custom_74hc283_1_s1, custom_74hc283_1_s2, custom_74hc283_1_s3, custom_74hc283_1_s4, multiplexer_1_out,
       multiplexer_2_out, multiplexer_3_out, multiplexer_4_out;

  custom_74HC161 A_74HC161 (
    .A(custom_74hc283_1_s1), .B(custom_74hc283_1_s2), .C(custom_74hc283_1_s3), .D(custom_74hc283_1_s4),
    .LD(in_1), .CK(CK), .QA(A_74HC161_qa), .QB(A_74HC161_qb), .QC(A_74HC161_qc), .QD(A_74HC161_qd));
  custom_74HC161 B_74HC161 (
    .A(custom_74hc283_1_s1), .B(custom_74hc283_1_s2), .C(custom_74hc283_1_s3), .D(custom_74hc283_1_s4),
    .LD(in_4), .CK(CK), .QA(B_74HC161_qa), .QB(B_74HC161_qb), .QC(B_74HC161_qc), .QD(B_74HC161_qd));
  custom_74HC161 C_74HC161 (
    .A(custom_74hc283_1_s1), .B(custom_74hc283_1_s2), .C(custom_74hc283_1_s3), .D(custom_74hc283_1_s4),
    .LD(in_7), .CK(CK), .QA(C_74HC161_qa), .QB(C_74HC161_qb), .QC(C_74HC161_qc), .QD(C_74HC161_qd));
  custom_74HC161 D_74HC161 (
    .A(custom_74hc283_1_s1), .B(custom_74hc283_1_s2), .C(custom_74hc283_1_s3), .D(custom_74hc283_1_s4),
    .LD(in_8), .CK(CK));  // open: QA, QB, QC, QD
  Multiplexer #(.select(2)) multiplexer_1 (
    .in0(A_74HC161_qa), .in1(B_74HC161_qa), .in2(C_74HC161_qa), .in3(1'b0), .out(multiplexer_1_out),
    .sel({B, A}));
  Multiplexer #(.select(2)) multiplexer_2 (
    .in0(A_74HC161_qb), .in1(B_74HC161_qb), .in2(C_74HC161_qb), .in3(1'b0), .out(multiplexer_2_out),
    .sel({B, A}));
  Multiplexer #(.select(2)) multiplexer_3 (
    .in0(A_74HC161_qc), .in1(B_74HC161_qc), .in2(C_74HC161_qc), .in3(1'b0), .out(multiplexer_3_out),
    .sel({B, A}));
  Multiplexer #(.select(2)) multiplexer_4 (
    .in0(A_74HC161_qd), .in1(B_74HC161_qd), .in2(C_74HC161_qd), .in3(1'b0), .out(multiplexer_4_out),
    .sel({2{A}}));
  custom_74HC283 custom_74hc283_1 (
    .A1(multiplexer_1_out), .B1(IM_1), .A2(multiplexer_2_out), .B2(IM_2), .A3(multiplexer_3_out), .B3(IM_3),
    .A4(multiplexer_4_out), .B4(IM_4), .S1(custom_74hc283_1_s1), .S2(custom_74hc283_1_s2),
    .S3(custom_74hc283_1_s3), .S4(custom_74hc283_1_s4), .C4(custom_74hc283_1_c4));
  D_Flip_Flop d_ff_1 (.D(custom_74hc283_1_c4), .clk(CK));  // open: Q, Qn, preset, reset
endmodule

module custom_74HC161 (
  input  A,
  input  B,
  input  C,
  input  D,
  input  LD,
  input  CK,
  output QA,
  output QB,
  output QC,
  output QD
);

  wire d_ff_1_qn, multiplexer_1_out, multiplexer_2_out, multiplexer_3_out, multiplexer_4_out, not_1_out;

  Multiplexer multiplexer_1 (.in0(QA), .in1(A), .out(multiplexer_1_out), .sel(not_1_out));
  Multiplexer multiplexer_2 (.in0(QB), .in1(B), .out(multiplexer_2_out), .sel(not_1_out));
  Multiplexer multiplexer_3 (.in0(QC), .in1(C), .out(multiplexer_3_out), .sel(not_1_out));
  Multiplexer multiplexer_4 (.in0(QD), .in1(D), .out(multiplexer_4_out), .sel(not_1_out));
  not not_1 (not_1_out, LD);
  D_Flip_Flop d_ff_1 (.D(multiplexer_1_out), .clk(CK), .Q(QA), .Qn(d_ff_1_qn));  // open: preset, reset
  D_Flip_Flop d_ff_2 (.D(multiplexer_2_out), .clk(CK), .Q(QB));  // open: Qn, preset, reset
  D_Flip_Flop d_ff_3 (.D(multiplexer_3_out), .clk(CK), .Q(QC));  // open: Qn, preset, reset
  D_Flip_Flop d_ff_4 (.D(multiplexer_4_out), .clk(CK), .Q(QD));  // open: Qn, preset, reset
endmodule

module custom_74HC283 (
  input  A1,
  input  B1,
  input  A2,
  input  B2,
  input  A3,
  input  B3,
  input  A4,
  input  B4,
  output S1,
  output S2,
  output S3,
  output S4,
  output C4
);

  wire adder_1_cout, adder_2_cout, adder_3_cout;

  Adder #(.width(1)) adder_1 (.a(A1), .b(B1), .out(S1), .cout(adder_1_cout));  // open: cin
  Adder #(.width(1)) adder_2 (.a(A2), .b(B2), .out(S2), .cin(adder_1_cout), .cout(adder_2_cout));
  Adder #(.width(1)) adder_3 (.a(A3), .b(B3), .out(S3), .cin(adder_2_cout), .cout(adder_3_cout));
  Adder #(.width(1)) adder_4 (.a(A4), .b(B4), .out(S4), .cin(adder_3_cout), .cout(C4));
endmodule
